// Logisim project DECODER.circ as structural Verilog: 1 circuit, main circuit main
module main (
  input  x,
  input  y,
  input  z
);

  wire and_1_out, and_2_out, and_3_out, and_4_out, and_5_out, and_6_out, and_7_out, and_8_out, and_9_out,
       and_10_out, and_11_out, and_12_out, and_13_out, and_14_out, and_15_out, and_16_out;

  and and_1 (and_1_out, x, z);
  and and_2 (and_2_out, ~x, ~z);  // AND_Gate
  and and_3 (and_3_out, y, z);
  and and_4 (and_4_out, ~y, ~z);  // AND_Gate
  and and_5 (and_5_out, x, ~y, z);  // AND_Gate
  and and_6 (and_6_out, y, ~z);  // AND_Gate
  and and_7 (and_7_out, ~x, y);  // AND_Gate
  and and_8 (and_8_out, ~x, ~z);  // AND_Gate
  and and_9 (and_9_out, y, ~z);  // AND_Gate
  and and_10 (and_10_out, ~x, ~z);  // AND_Gate
  and and_11 (and_11_out, ~y, ~z);  // AND_Gate
  and and_12 (and_12_out, x, ~y);  // AND_Gate
  and and_13 (and_13_out, x, ~z);  // AND_Gate
  and and_14 (and_14_out, x, ~y);  // AND_Gate
  and and_15 (and_15_out, ~x, y);  // AND_Gate
  and and_16 (and_16_out, y, ~z);  // AND_Gate
  // OR_Gate a has open pins: in0=and_1_out, in1=y, in2=and_2_out, out=open
  // OR_Gate b has open pins: in0=x, in1=and_3_out, in2=and_4_out, out=open
  // OR_Gate c has open pins: in0=x, in1=y, in2=z, out=open
  // OR_Gate d has open pins: in0=and_5_out, in1=and_6_out, in2=and_7_out, in3=and_8_out, out=open
  // OR_Gate e has open pins: in0=and_9_out, in2=and_10_out, out=open
  // OR_Gate f has open pins: in0=and_11_out, in1=and_12_out, in2=and_13_out, out=open
  // OR_Gate g has open pins: in0=and_14_out, in1=and_15_out, in2=and_16_out, out=open
endmodule
