// Logisim project Voting Card Reader Design - CIRCUIT.circ as structural Verilog: 2 circuits, main circuit main
module main (
  input  in_1,
  input  in_2,
  input  in_3,
  input  in_4,
  input  in_5,
  input  in_6,
  input  User_input
);

  wire a_out, and_1_out, and_2_out, and_3_out, and_4_out, and_5_out, and_6_out, and_7_out, and_8_out,
       and_9_out, and_10_out, and_11_out, and_12_out, and_13_out, and_14_out, and_15_out, and_16_out, b_out,
       c_out, d_out, e_out, encoder_1_out_8, encoder_1_out_9, encoder_1_out_10, f_out, g_out;

  encoder encoder_1 (
    .Y1(in_1), .Y2(in_2), .Y3(in_3), .Y4(in_4), .Y5(in_5), .Y6(in_6), .Y7(User_input),
    .out_8(encoder_1_out_8), .out_9(encoder_1_out_9), .out_10(encoder_1_out_10));
  and and_1 (and_1_out, encoder_1_out_8, encoder_1_out_10);
  and and_2 (and_2_out, ~encoder_1_out_8, ~encoder_1_out_10);  // AND_Gate
  and and_3 (and_3_out, encoder_1_out_9, encoder_1_out_10);
  and and_4 (and_4_out, ~encoder_1_out_9, ~encoder_1_out_10);  // AND_Gate
  and and_5 (and_5_out, encoder_1_out_8, ~encoder_1_out_9, encoder_1_out_10);  // AND_Gate
  and and_6 (and_6_out, encoder_1_out_9, ~encoder_1_out_10);  // AND_Gate
  and and_7 (and_7_out, ~encoder_1_out_8, encoder_1_out_9);  // AND_Gate
  and and_8 (and_8_out, ~encoder_1_out_8, ~encoder_1_out_10);  // AND_Gate
  and and_9 (and_9_out, encoder_1_out_9, ~encoder_1_out_10);  // AND_Gate
  and and_10 (and_10_out, ~encoder_1_out_8, ~encoder_1_out_10);  // AND_Gate
  and and_11 (and_11_out, ~encoder_1_out_9, ~encoder_1_out_10);  // AND_Gate
  and and_12 (and_12_out, encoder_1_out_8, ~encoder_1_out_9);  // AND_Gate
  and and_13 (and_13_out, encoder_1_out_8, ~encoder_1_out_10);  // AND_Gate
  and and_14 (and_14_out, encoder_1_out_8, ~encoder_1_out_9);  // AND_Gate
  and and_15 (and_15_out, ~encoder_1_out_8, encoder_1_out_9);  // AND_Gate
  and and_16 (and_16_out, encoder_1_out_9, ~encoder_1_out_10);  // AND_Gate
  or a (a_out, and_1_out, encoder_1_out_9, and_2_out);
  or b (b_out, ~encoder_1_out_8, and_3_out, and_4_out);  // OR_Gate
  or c (c_out, encoder_1_out_8, ~encoder_1_out_9, encoder_1_out_10);  // OR_Gate
  or d (d_out, and_5_out, and_6_out, and_7_out, and_8_out);
  or e (e_out, and_9_out, and_10_out);
  or f (f_out, and_11_out, and_12_out, and_13_out);
  or g (g_out, and_14_out, and_15_out, and_16_out);
  _7_Segment_Display u_7_segment_display_1 (
    .g(g_out), .f(f_out), .a(a_out), .b(b_out), .e(e_out), .d(d_out), .c(c_out));  // open: dp

  // Notes on the sheet:
  //   Encoder
  //   Decoder Circuit below
  //   Output
endmodule

module encoder (
  input  Y1,
  input  Y2,
  input  Y3,
  input  Y4,
  input  Y5,
  input  Y6,
  input  Y7,
  output out_8,
  output out_9,
  output out_10
);

  wire A0_out, A1_out, A2_out, xor_1_out;

  or A2 (A2_out, Y7, Y6, Y5, Y4);
  or A1 (A1_out, Y7, Y6, Y3, Y2);
  or A0 (A0_out, Y7, Y5, Y3, Y1);
  ExactlyOne xor_1 (.out(xor_1_out), .in0(Y7), .in1(Y6), .in2(Y5), .in3(Y4), .in4(Y3), .in5(Y2), .in6(Y1));
  and and_1 (out_8, A2_out, xor_1_out);
  and and_2 (out_9, A1_out, xor_1_out);
  and and_3 (out_10, A0_out, xor_1_out);

  // Notes on the sheet:
  //   XOR gate has a function to control MAX one input from user.
endmodule
